# Fritzing sketch Wendy numbers (saved by Fritzing 0.9.3b)
breadboards: 2

parts:
  Part1 = Arduino Uno (Rev3)
  btnZero = Pushbutton [package="[THT]"]
  btnOne = Pushbutton [package="[THT]"]
  btnTwo = Pushbutton [package="[THT]"]
  btnThree = Pushbutton [package="[THT]"]
  btnFour = Pushbutton [package="[THT]"]
  btnFive = Pushbutton [package="[THT]"]
  btnSix = Pushbutton [package="[THT]"]
  btnSeven = Pushbutton [package="[THT]"]
  btnEight = Pushbutton [package="[THT]"]
  btnNine = Pushbutton [package="[THT]"]
  R1 = Resistor [tolerance=±5% resistance=1M package=THT]
  R2 = Resistor [tolerance=±5% resistance=1M package=THT]
  R3 = Resistor [tolerance=±5% resistance=1M package=THT]
  R4 = Resistor [tolerance=±5% resistance=1M package=THT]
  R5 = Resistor [tolerance=±5% resistance=1M package=THT]
  R6 = Resistor [tolerance=±5% resistance=1M package=THT]
  R7 = Resistor [tolerance=±5% resistance=1M package=THT]
  R8 = Resistor [tolerance=±5% resistance=1M package=THT]
  R9 = Resistor [tolerance=±5% resistance=1M package=THT]
  R10 = Resistor [tolerance=±5% resistance=1M package=THT]
  R11 = Rotary Potentiometer (Small) [maximum_resistance=100kΩ package=THT]
  R12 = Resistor [tolerance=±5% resistance=220 package=THT]
  LCD1 = LCD screen

nets:
  N1: Part1.A0, btnZero.Pin_1, btnZero.Pin_2, R1.Pin_0
  N2: Part1.A1, btnOne.Pin_1, btnOne.Pin_2, R2.Pin_0
  N3: Part1.A2, btnTwo.Pin_1, btnTwo.Pin_2, R3.Pin_0
  N4: Part1.A3, btnThree.Pin_1, btnThree.Pin_2, R4.Pin_0
  N5: Part1.A4/SDA, btnFour.Pin_1, btnFour.Pin_2, R5.Pin_0
  N6: Part1.A5/SCL, btnFive.Pin_1, btnFive.Pin_2, R6.Pin_0
  N7: Part1.D8, btnEight.Pin_1, btnEight.Pin_2, R9.Pin_0
  N8: Part1.D9_PWM, btnNine.Pin_1, btnNine.Pin_2, R10.Pin_0
  N9: Part1.D11_PWM/MOSI, LCD1.E
  N10: Part1.D12/MISO, LCD1.RS
  GND: Part1.GND, R1.Pin_1, R2.Pin_1, R3.Pin_1, R4.Pin_1, R5.Pin_1, R6.Pin_1, R7.Pin_1, R8.Pin_1, R9.Pin_1, R10.Pin_1, R11.leg1, LCD1.VSS, LCD1.R/W, LCD1.LED-
  N11: Part1.D2, LCD1.DB7
  N12: Part1.D3_PWM, LCD1.DB6
  N13: Part1.D4, LCD1.DB5
  N14: Part1.D5_PWM, LCD1.DB4
  N15: Part1.D6_PWM, btnSix.Pin_1, btnSix.Pin_2, R7.Pin_0
  N16: Part1.D7, btnSeven.Pin_1, btnSeven.Pin_2, R8.Pin_0
  5V: Part1.5V, btnZero.Pin_3, btnZero.Pin_4, btnOne.Pin_3, btnOne.Pin_4, btnTwo.Pin_3, btnTwo.Pin_4, btnThree.Pin_3, btnThree.Pin_4, btnFour.Pin_3, btnFour.Pin_4, btnFive.Pin_3, btnFive.Pin_4, btnSix.Pin_3, btnSix.Pin_4, btnSeven.Pin_3, btnSeven.Pin_4, btnEight.Pin_3, btnEight.Pin_4, btnNine.Pin_3, btnNine.Pin_4, R11.leg2, R12.Pin_1, LCD1.VDD
  N17: R11.wiper, LCD1.V0
  N18: R12.Pin_0, LCD1.LED+
